// Logisim project SaguiVetorial.circ as structural Verilog: 14 circuits, main circuit UC
module main (
);

  wire botao, c, I, PC_src, R1, rg, vetorial0_1_cc, vetorial0_1_wmv, vetorial1_1_cc, vetorial1_1_wmv,
       vetorial2_1_cc, vetorial2_1_wmv, vetorial3_1_cc, vetorial3_1_wmv, WM, WREG, zero;
  wire [2:0] ULA_op;
  wire [3:0] imm;
  wire [7:0] adder_1_out, multiplexer_1_out, opB, ram_1_dout, ram_2_dout, ram_3_dout, ram_4_dout,
       register_1_q, vetorial0_1_opa, vetorial0_1_opb, vetorial1_1_opa, vetorial1_1_opb, vetorial2_1_opa,
       vetorial2_1_opb, vetorial3_1_opa, vetorial3_1_opb;
  wire [7:4] rom_1_data;

  // Probe on PC_src
  // Probe on multiplexer_1_out
  Multiplexer #(.width(8)) multiplexer_1 (.in0(adder_1_out), .in1(opB), .out(multiplexer_1_out), .sel(PC_src));
  Clock clock_1 (.out(c));
  Register register_1 (.D(multiplexer_1_out), .en(1'b1), .clk(c), .Q(register_1_q), .clr(botao));
  Button button_1 (.out(botao));
  // Probe on register_1_q
  ROM rom_1 (.addr(register_1_q), .data({rom_1_data, imm}));
  Adder adder_1 (.a(register_1_q), .b(8'h1), .out(adder_1_out));  // open: cin, cout
  UCM ucm_1 (
    .inst({rom_1_data, imm}), .zero(zero), .ULA_op(ULA_op), .WREG(WREG), .I(I), .R1(R1), .rg(rg), .WM(WM),
    .PC_src(PC_src));
  Vetorial0 vetorial0_1 (
    .botao(botao), .WREG(WREG), .BS(rom_1_data[7]), .c(c), .R1(R1), .imm(imm), .I(I), .ula_op(ULA_op),
    .WM(WM), .rg(rg), .regs(imm), .D(ram_1_dout), .opB(vetorial0_1_opb), .WMv(vetorial0_1_wmv),
    .cc(vetorial0_1_cc), .opA(vetorial0_1_opa));
  vetorial1 vetorial1_1 (
    .botao(botao), .WREG(WREG), .BS(rom_1_data[7]), .c(c), .R1(R1), .imm(imm), .I(I), .ula_op(ULA_op),
    .WM(WM), .rg(rg), .regs(imm), .D(ram_2_dout), .opB(vetorial1_1_opb), .WMv(vetorial1_1_wmv),
    .cc(vetorial1_1_cc), .opA(vetorial1_1_opa));
  Escalar escalar_1 (
    .botao(botao), .WREG(WREG), .BS(rom_1_data[7]), .c(c), .R1(R1), .imm(imm), .I(I), .ula_op(ULA_op),
    .WM(WM), .rg(rg), .regs(imm), .zero(zero), .opB(opB));
  RAM #(.enables("line")) ram_1 (
    .addr(vetorial0_1_opb), .we(vetorial0_1_wmv), .clk(vetorial0_1_cc), .din(vetorial0_1_opa),
    .dout(ram_1_dout));
  RAM #(.enables("line")) ram_2 (
    .addr(vetorial1_1_opb), .we(vetorial1_1_wmv), .clk(vetorial1_1_cc), .din(vetorial1_1_opa),
    .dout(ram_2_dout));
  vetorial2 vetorial2_1 (
    .botao(botao), .WREG(WREG), .BS(rom_1_data[7]), .c(c), .R1(R1), .imm(imm), .I(I), .ula_op(ULA_op),
    .WM(WM), .rg(rg), .regs(imm), .D(ram_3_dout), .opB(vetorial2_1_opb), .WMv(vetorial2_1_wmv),
    .cc(vetorial2_1_cc), .opA(vetorial2_1_opa));
  vetorial3 vetorial3_1 (
    .botao(botao), .WREG(WREG), .BS(rom_1_data[7]), .c(c), .R1(R1), .imm(imm), .I(I), .ula_op(ULA_op),
    .WM(WM), .rg(rg), .regs(imm), .D(ram_4_dout), .opB(vetorial3_1_opb), .WMv(vetorial3_1_wmv),
    .cc(vetorial3_1_cc), .opA(vetorial3_1_opa));
  RAM #(.enables("line")) ram_3 (
    .addr(vetorial2_1_opb), .we(vetorial2_1_wmv), .clk(vetorial2_1_cc), .din(vetorial2_1_opa),
    .dout(ram_3_dout));
  RAM #(.enables("line")) ram_4 (
    .addr(vetorial3_1_opb), .we(vetorial3_1_wmv), .clk(vetorial3_1_cc), .din(vetorial3_1_opa),
    .dout(ram_4_dout));

  // Notes on the sheet:
  //   contents of rom_1 (hex, n*v repeats v):
  //   20 32 49 31 4d 90 a0 b4 c9 c4 21 33 79 95 c6 5b 20 3a 71 20 33 49 cd a1 b4 c4 22 34 79 97 ce c6 5b
  //   21 3a 71 20 33 49 a0 b0 23 32 79 97 ce 5b 22 39 71 20 33 49 da c8 24 3d 79 8e a0 bc c9 86 cd a0 bc
  //   c9 9e c5 d9 a0 b4 c9 5b 23 37 71 24 3f 71
endmodule

module UC (
  input  [7:0] in_1,
  output [2:0] ula_op,
  output ld,
  output b,
  output st,
  output I
);

  wire mh, ml, or_2_out, ou;

  and and_1 (b, in_1[4], in_1[5], in_1[6], ~in_1[7]);  // AND_Gate
  and and_2 (ld, ~in_1[4], ~in_1[5], ~in_1[6]);  // AND_Gate
  and and_3 (st, in_1[4], ~in_1[5], ~in_1[6]);  // AND_Gate
  and and_4 (mh, ~in_1[4], in_1[5], ~in_1[6]);  // AND_Gate
  and and_5 (ml, in_1[4], in_1[5], ~in_1[6]);  // AND_Gate
  and and_6 (ou, in_1[4], in_1[5], in_1[6], in_1[7]);
  or or_1 (I, mh, ml);
  Multiplexer #(.width(3)) multiplexer_1 (.in0(in_1[6:4]), .in1({2'b00, in_1[7]}), .out(ula_op), .sel(or_2_out));
  or or_2 (or_2_out, b, ou);

  // Other names for the same wires on the sheet: a0 = in_1[4]; opcode[3:0] = in_1[7:4]; a1 = in_1[5]; a2 = in_1[6];
  //   a3 = in_1[7]; imm[3:0] = in_1[3:0]
endmodule

module BdR (
  input  [7:0] Din,
  input  [1:0] ra,
  input  C,
  input  botao,
  input  WE,
  input  [1:0] rb,
  input  [1:0] rw,
  output [7:0] Da,
  output [7:0] Db
);

  wire demultiplexer_1_out1, demultiplexer_1_out2, demultiplexer_1_out3;
  wire [7:0] register_1_q, register_2_q, register_3_q, register_4_q;

  Demultiplexer #(.select(2)) demultiplexer_1 (
    .out1(demultiplexer_1_out1), .out2(demultiplexer_1_out2), .out3(demultiplexer_1_out3), .in(WE), .sel(rw));  // open: out0
  Register register_1 (.D({8{1'b0}}), .en(1'b1), .clk(C), .Q(register_1_q));  // open: clr
  Register register_2 (.D(Din), .en(demultiplexer_1_out1), .clk(C), .Q(register_2_q), .clr(botao));
  Register register_3 (.D(Din), .en(demultiplexer_1_out2), .clk(C), .Q(register_3_q), .clr(botao));
  Register register_4 (.D(Din), .en(demultiplexer_1_out3), .clk(C), .Q(register_4_q), .clr(botao));
  Multiplexer #(.select(2), .width(8)) multiplexer_1 (
    .in0(register_1_q), .in1(register_2_q), .in2(register_3_q), .in3(register_4_q), .out(Da), .sel(ra));
  Multiplexer #(.select(2), .width(8)) multiplexer_2 (
    .in0(register_1_q), .in1(register_2_q), .in2(register_3_q), .in3(register_4_q), .out(Db), .sel(rb));
endmodule

module ULA (
  input  [7:0] opA,
  input  [7:0] opB,
  input  [2:0] ULA_op,
  output zero,
  output [7:0] R
);

  wire comparator_1_eq;
  wire [7:0] adder_1_out, and_1_out, bit_extender_1_out, or_1_out, subtractor_1_out;

  Comparator comparator_1 (.a(opA), .b({8{1'b0}}), .eq(comparator_1_eq));  // open: gt, lt
  assign or_1_out = opA | opB;  // OR_Gate or_1, 8 bits wide
  Adder adder_1 (.a(opA), .b(opB), .out(adder_1_out));  // open: cin, cout
  Subtractor subtractor_1 (.a(opA), .b(opB), .out(subtractor_1_out));  // open: bin, bout
  assign and_1_out = opA & opB;  // AND_Gate and_1, 8 bits wide
  assign bit_extender_1_out = {{7{comparator_1_eq}}, comparator_1_eq};  // Bit_Extender bit_extender_1
  Multiplexer #(.select(3), .width(8)) multiplexer_1 (
    .in0(bit_extender_1_out), .in1(or_1_out), .in2({opB[3:0], opA[3:0]}), .in3({opA[7:4], opB[3:0]}),
    .in4(adder_1_out), .in5(subtractor_1_out), .in6(and_1_out), .in7(and_1_out), .out(R), .sel(ULA_op));
  Comparator comparator_2 (.a(R), .b({8{1'b0}}), .eq(zero));  // open: gt, lt
endmodule

module UCM (
  input  [7:0] inst,
  input  zero,
  output [2:0] ULA_op,
  output WREG,
  output I,
  output R1,
  output rg,
  output WM,
  output PC_src
);

  wire b;

  UC uc_1 (.in_1(inst), .ula_op(ULA_op), .ld(rg), .b(b), .st(WM), .I(I));
  and and_1 (WREG, ~WM, ~b);  // AND_Gate
  and and_2 (PC_src, b, ~zero);  // AND_Gate

  assign R1 = I;

  // Other names for the same wires on the sheet: ld = rg; st = WM
endmodule

module Escalar (
  input  botao,
  input  WREG,
  input  BS,
  input  c,
  input  R1,
  input  [3:0] imm,
  input  I,
  input  [2:0] ula_op,
  input  WM,
  input  rg,
  input  [3:0] regs,
  output zero,
  output [7:0] opB
);

  wire and_1_out, and_2_out;
  wire [1:0] multiplexer_1_out;
  wire [7:0] bit_extender_1_out, multiplexer_2_out, multiplexer_3_out, opA, ram_1_dout, ula_1_r;

  // Probe on multiplexer_1_out
  Multiplexer #(.width(2)) multiplexer_1 (.in0(regs[3:2]), .in1(2'b01), .out(multiplexer_1_out), .sel(R1));
  // Probe on regs[1:0]
  and and_1 (and_1_out, WREG, ~BS);  // AND_Gate
  // Probe on opA
  BdR bdr_1 (
    .Din(multiplexer_3_out), .ra(multiplexer_1_out), .C(c), .botao(botao), .WE(and_1_out), .rb(regs[1:0]),
    .rw(multiplexer_1_out), .Da(opA), .Db(opB));
  // Probe on multiplexer_3_out
  assign bit_extender_1_out = {{4{imm[3]}}, imm};  // Bit_Extender bit_extender_1
  // Probe on opB
  Multiplexer #(.width(8)) multiplexer_2 (.in0(opB), .in1(bit_extender_1_out), .out(multiplexer_2_out), .sel(I));
  Multiplexer #(.width(8)) multiplexer_3 (.in0(ula_1_r), .in1(ram_1_dout), .out(multiplexer_3_out), .sel(rg));
  // Probe on ula_op
  // Probe on ula_1_r
  ULA ula_1 (.opA(opA), .opB(multiplexer_2_out), .ULA_op(ula_op), .zero(zero), .R(ula_1_r));
  and and_2 (and_2_out, WM, ~BS);  // AND_Gate
  RAM #(.enables("line")) ram_1 (.addr(opB), .we(and_2_out), .clk(c), .din(opA), .dout(ram_1_dout));
endmodule

module Vetorial0 (
  input  botao,
  input  WREG,
  input  BS,
  input  c,
  input  R1,
  input  [3:0] imm,
  input  I,
  input  [2:0] ula_op,
  input  WM,
  input  rg,
  input  [3:0] regs,
  input  [7:0] D,
  output [7:0] opB,
  output WMv,
  output cc,
  output [7:0] opA
);

  wire and_1_out, zero;
  wire [1:0] multiplexer_1_out;
  wire [7:0] bit_extender_1_out, multiplexer_2_out, multiplexer_3_out, ula_1_r;

  // Probe on multiplexer_1_out
  Multiplexer #(.width(2)) multiplexer_1 (.in0(regs[3:2]), .in1(2'b01), .out(multiplexer_1_out), .sel(R1));
  // Probe on regs[1:0]
  and and_1 (and_1_out, WREG, BS);
  // Probe on opA
  BdR0 bdr0_1 (
    .Din(multiplexer_3_out), .ra(multiplexer_1_out), .C(c), .botao(botao), .WE(and_1_out), .rb(regs[1:0]),
    .rw(multiplexer_1_out), .Da(opA), .Db(opB));
  // Probe on multiplexer_3_out
  assign bit_extender_1_out = {{4{imm[3]}}, imm};  // Bit_Extender bit_extender_1
  // Probe on opB
  Multiplexer #(.width(8)) multiplexer_2 (.in0(opB), .in1(bit_extender_1_out), .out(multiplexer_2_out), .sel(I));
  Multiplexer #(.width(8)) multiplexer_3 (.in0(ula_1_r), .in1(D), .out(multiplexer_3_out), .sel(rg));
  // Probe on ula_op
  // Probe on ula_1_r
  ULA ula_1 (.opA(opA), .opB(multiplexer_2_out), .ULA_op(ula_op), .zero(zero), .R(ula_1_r));
  and and_2 (WMv, WM, BS);

  assign cc = c;
endmodule

module vetorial1 (
  input  botao,
  input  WREG,
  input  BS,
  input  c,
  input  R1,
  input  [3:0] imm,
  input  I,
  input  [2:0] ula_op,
  input  WM,
  input  rg,
  input  [3:0] regs,
  input  [7:0] D,
  output [7:0] opB,
  output WMv,
  output cc,
  output [7:0] opA
);

  wire and_1_out, undriven, zero;
  wire [1:0] multiplexer_1_out;
  wire [7:0] bit_extender_1_out, multiplexer_2_out, multiplexer_3_out, ula_1_r;

  // Probe on multiplexer_1_out
  Multiplexer #(.width(2)) multiplexer_1 (.in0(regs[3:2]), .in1(2'b01), .out(multiplexer_1_out), .sel(R1));
  // Probe on undriven
  and and_1 (and_1_out, WREG, BS);
  // Probe on opA
  BdR1 bdr1_1 (
    .Din(multiplexer_3_out), .ra(multiplexer_1_out), .C(c), .botao(botao), .WE(and_1_out), .rb(regs[1:0]),
    .rw(multiplexer_1_out), .Da(opA), .Db(opB));
  // Probe on multiplexer_3_out
  assign bit_extender_1_out = {{4{imm[3]}}, imm};  // Bit_Extender bit_extender_1
  // Probe on opB
  Multiplexer #(.width(8)) multiplexer_2 (.in0(opB), .in1(bit_extender_1_out), .out(multiplexer_2_out), .sel(I));
  Multiplexer #(.width(8)) multiplexer_3 (.in0(ula_1_r), .in1(D), .out(multiplexer_3_out), .sel(rg));
  // Probe on ula_op
  // Probe on ula_1_r
  ULA ula_1 (.opA(opA), .opB(multiplexer_2_out), .ULA_op(ula_op), .zero(zero), .R(ula_1_r));
  and and_2 (WMv, WM, BS);

  assign cc = c;
endmodule

module vetorial2 (
  input  botao,
  input  WREG,
  input  BS,
  input  c,
  input  R1,
  input  [3:0] imm,
  input  I,
  input  [2:0] ula_op,
  input  WM,
  input  rg,
  input  [3:0] regs,
  input  [7:0] D,
  output [7:0] opB,
  output WMv,
  output cc,
  output [7:0] opA
);

  wire and_1_out, undriven, zero;
  wire [1:0] multiplexer_1_out;
  wire [7:0] bit_extender_1_out, multiplexer_2_out, multiplexer_3_out, ula_1_r;

  // Probe on multiplexer_1_out
  Multiplexer #(.width(2)) multiplexer_1 (.in0(regs[3:2]), .in1(2'b01), .out(multiplexer_1_out), .sel(R1));
  // Probe on undriven
  and and_1 (and_1_out, WREG, BS);
  // Probe on opA
  BdR2 bdr2_1 (
    .Din(multiplexer_3_out), .ra(multiplexer_1_out), .C(c), .botao(botao), .WE(and_1_out), .rb(regs[1:0]),
    .rw(multiplexer_1_out), .Da(opA), .Db(opB));
  // Probe on multiplexer_3_out
  assign bit_extender_1_out = {{4{imm[3]}}, imm};  // Bit_Extender bit_extender_1
  // Probe on opB
  Multiplexer #(.width(8)) multiplexer_2 (.in0(opB), .in1(bit_extender_1_out), .out(multiplexer_2_out), .sel(I));
  Multiplexer #(.width(8)) multiplexer_3 (.in0(ula_1_r), .in1(D), .out(multiplexer_3_out), .sel(rg));
  // Probe on ula_op
  // Probe on ula_1_r
  ULA ula_1 (.opA(opA), .opB(multiplexer_2_out), .ULA_op(ula_op), .zero(zero), .R(ula_1_r));
  and and_2 (WMv, WM, BS);

  assign cc = c;
endmodule

module vetorial3 (
  input  botao,
  input  WREG,
  input  BS,
  input  c,
  input  R1,
  input  [3:0] imm,
  input  I,
  input  [2:0] ula_op,
  input  WM,
  input  rg,
  input  [3:0] regs,
  input  [7:0] D,
  output [7:0] opB,
  output WMv,
  output cc,
  output [7:0] opA
);

  wire and_1_out, undriven, zero;
  wire [1:0] multiplexer_1_out;
  wire [7:0] bit_extender_1_out, multiplexer_2_out, multiplexer_3_out, ula_1_r;

  // Probe on multiplexer_1_out
  Multiplexer #(.width(2)) multiplexer_1 (.in0(regs[3:2]), .in1(2'b01), .out(multiplexer_1_out), .sel(R1));
  // Probe on undriven
  and and_1 (and_1_out, WREG, BS);
  // Probe on opA
  BdR3 bdr3_1 (
    .Din(multiplexer_3_out), .ra(multiplexer_1_out), .C(c), .botao(botao), .WE(and_1_out), .rb(regs[1:0]),
    .rw(multiplexer_1_out), .Da(opA), .Db(opB));
  // Probe on multiplexer_3_out
  assign bit_extender_1_out = {{4{imm[3]}}, imm};  // Bit_Extender bit_extender_1
  // Probe on opB
  Multiplexer #(.width(8)) multiplexer_2 (.in0(opB), .in1(bit_extender_1_out), .out(multiplexer_2_out), .sel(I));
  Multiplexer #(.width(8)) multiplexer_3 (.in0(ula_1_r), .in1(D), .out(multiplexer_3_out), .sel(rg));
  // Probe on ula_op
  // Probe on ula_1_r
  ULA ula_1 (.opA(opA), .opB(multiplexer_2_out), .ULA_op(ula_op), .zero(zero), .R(ula_1_r));
  and and_2 (WMv, WM, BS);

  assign cc = c;
endmodule

module BdR0 (
  input  [7:0] Din,
  input  [1:0] ra,
  input  C,
  input  botao,
  input  WE,
  input  [1:0] rb,
  input  [1:0] rw,
  output [7:0] Da,
  output [7:0] Db
);

  wire demultiplexer_1_out1, demultiplexer_1_out2, demultiplexer_1_out3;
  wire [7:0] register_1_q, register_2_q, register_3_q, register_4_q;

  Demultiplexer #(.select(2)) demultiplexer_1 (
    .out1(demultiplexer_1_out1), .out2(demultiplexer_1_out2), .out3(demultiplexer_1_out3), .in(WE), .sel(rw));  // open: out0
  Register register_1 (.D({8{1'b0}}), .en(1'b1), .clk(C), .Q(register_1_q));  // open: clr
  Register register_2 (.D(Din), .en(demultiplexer_1_out1), .clk(C), .Q(register_2_q), .clr(botao));
  Register register_3 (.D(Din), .en(demultiplexer_1_out2), .clk(C), .Q(register_3_q), .clr(botao));
  Register register_4 (.D(Din), .en(demultiplexer_1_out3), .clk(C), .Q(register_4_q), .clr(botao));
  // Probe on register_4_q
  // Probe on Da
  Multiplexer #(.select(2), .width(8)) multiplexer_1 (
    .in0(register_1_q), .in1(register_2_q), .in2(register_3_q), .in3(register_4_q), .out(Da), .sel(ra));
  Multiplexer #(.select(2), .width(8)) multiplexer_2 (
    .in0(register_1_q), .in1(register_2_q), .in2(register_3_q), .in3(register_4_q), .out(Db), .sel(rb));
  // Probe on Db
endmodule

module BdR1 (
  input  [7:0] Din,
  input  [1:0] ra,
  input  C,
  input  botao,
  input  WE,
  input  [1:0] rb,
  input  [1:0] rw,
  output [7:0] Da,
  output [7:0] Db
);

  wire demultiplexer_1_out1, demultiplexer_1_out2, demultiplexer_1_out3;
  wire [7:0] register_1_q, register_2_q, register_3_q, register_4_q;

  Demultiplexer #(.select(2)) demultiplexer_1 (
    .out1(demultiplexer_1_out1), .out2(demultiplexer_1_out2), .out3(demultiplexer_1_out3), .in(WE), .sel(rw));  // open: out0
  Register register_1 (.D(8'h1), .en(1'b1), .clk(C), .Q(register_1_q));  // open: clr
  Register register_2 (.D(Din), .en(demultiplexer_1_out1), .clk(C), .Q(register_2_q), .clr(botao));
  Register register_3 (.D(Din), .en(demultiplexer_1_out2), .clk(C), .Q(register_3_q), .clr(botao));
  Register register_4 (.D(Din), .en(demultiplexer_1_out3), .clk(C), .Q(register_4_q), .clr(botao));
  Multiplexer #(.select(2), .width(8)) multiplexer_1 (
    .in0(register_1_q), .in1(register_2_q), .in2(register_3_q), .in3(register_4_q), .out(Da), .sel(ra));
  Multiplexer #(.select(2), .width(8)) multiplexer_2 (
    .in0(register_1_q), .in1(register_2_q), .in2(register_3_q), .in3(register_4_q), .out(Db), .sel(rb));
endmodule

module BdR2 (
  input  [7:0] Din,
  input  [1:0] ra,
  input  C,
  input  botao,
  input  WE,
  input  [1:0] rb,
  input  [1:0] rw,
  output [7:0] Da,
  output [7:0] Db
);

  wire demultiplexer_1_out1, demultiplexer_1_out2, demultiplexer_1_out3;
  wire [7:0] register_1_q, register_2_q, register_3_q, register_4_q;

  Demultiplexer #(.select(2)) demultiplexer_1 (
    .out1(demultiplexer_1_out1), .out2(demultiplexer_1_out2), .out3(demultiplexer_1_out3), .in(WE), .sel(rw));  // open: out0
  Register register_1 (.D(8'h2), .en(1'b1), .clk(C), .Q(register_1_q));  // open: clr
  Register register_2 (.D(Din), .en(demultiplexer_1_out1), .clk(C), .Q(register_2_q), .clr(botao));
  Register register_3 (.D(Din), .en(demultiplexer_1_out2), .clk(C), .Q(register_3_q), .clr(botao));
  Register register_4 (.D(Din), .en(demultiplexer_1_out3), .clk(C), .Q(register_4_q), .clr(botao));
  Multiplexer #(.select(2), .width(8)) multiplexer_1 (
    .in0(register_1_q), .in1(register_2_q), .in2(register_3_q), .in3(register_4_q), .out(Da), .sel(ra));
  Multiplexer #(.select(2), .width(8)) multiplexer_2 (
    .in0(register_1_q), .in1(register_2_q), .in2(register_3_q), .in3(register_4_q), .out(Db), .sel(rb));
endmodule

module BdR3 (
  input  [7:0] Din,
  input  [1:0] ra,
  input  C,
  input  botao,
  input  WE,
  input  [1:0] rb,
  input  [1:0] rw,
  output [7:0] Da,
  output [7:0] Db
);

  wire demultiplexer_1_out1, demultiplexer_1_out2, demultiplexer_1_out3;
  wire [7:0] register_1_q, register_2_q, register_3_q, register_4_q;

  Demultiplexer #(.select(2)) demultiplexer_1 (
    .out1(demultiplexer_1_out1), .out2(demultiplexer_1_out2), .out3(demultiplexer_1_out3), .in(WE), .sel(rw));  // open: out0
  Register register_1 (.D(8'h3), .en(1'b1), .clk(C), .Q(register_1_q));  // open: clr
  Register register_2 (.D(Din), .en(demultiplexer_1_out1), .clk(C), .Q(register_2_q), .clr(botao));
  Register register_3 (.D(Din), .en(demultiplexer_1_out2), .clk(C), .Q(register_3_q), .clr(botao));
  Register register_4 (.D(Din), .en(demultiplexer_1_out3), .clk(C), .Q(register_4_q), .clr(botao));
  // Probe on register_4_q
  Multiplexer #(.select(2), .width(8)) multiplexer_1 (
    .in0(register_1_q), .in1(register_2_q), .in2(register_3_q), .in3(register_4_q), .out(Da), .sel(ra));
  Multiplexer #(.select(2), .width(8)) multiplexer_2 (
    .in0(register_1_q), .in1(register_2_q), .in2(register_3_q), .in3(register_4_q), .out(Db), .sel(rb));
endmodule
